# Fritzing sketch Circuit (saved by Fritzing 0.9.3b)
breadboards: 1

parts:
  Part1 = Arduino Uno (Rev3) - ICSP
  S1 = Pushbutton [package="[THT]"]
  S2 = Pushbutton [package="[THT]"]
  S3 = Pushbutton [package="[THT]"]
  S4 = Pushbutton [package="[THT]"]
  S5 = Pushbutton [package="[THT]"]
  S6 = Pushbutton [package="[THT]"]
  R1 = Resistor [tolerance=±5% resistance=10k package="2512 [SMD]"]
  R2 = Resistor [tolerance=±5% resistance=10k package="2512 [SMD]"]
  R3 = Resistor [tolerance=±5% resistance=10k package="2512 [SMD]"]
  R4 = Resistor [tolerance=±5% resistance=10k package="2512 [SMD]"]
  R5 = Resistor [tolerance=±5% resistance=10k package="2512 [SMD]"]
  R6 = Resistor [tolerance=±5% resistance=10k package="2512 [SMD]"]
  LED1 = LED - 5mm [color="Red (633nm)" package="5 mm [THT]"]
  LED2 = LED - 5mm [color="Green (565nm)" package="5 mm [THT]"]
  R7 = Resistor [tolerance=±5% resistance=220 package=THT]
  R8 = Resistor [tolerance=±5% resistance=220 package=THT]
  J1 = Basic Servo

nets:
  N1: Part1.ICSP_MISO, Part1.D12/MISO, R7.Pin_1
  N2: Part1.D8, S6.Pin_1, S6.Pin_2, R6.Pin_0
  N3: Part1.D9_PWM, J1.pulse
  N4: Part1.D11_PWM/MOSI, R8.Pin_1
  N5: Part1.AREF, LED1.cathode, LED2.cathode, J1.gnd
  N6: Part1.D2, S1.Pin_1, S1.Pin_2, R1.Pin_0
  N7: Part1.D3_PWM, S2.Pin_1, S2.Pin_2, R2.Pin_0
  N8: Part1.D4, S3.Pin_1, S3.Pin_2, R3.Pin_0
  N9: Part1.D5_PWM, S4.Pin_1, S4.Pin_2, R4.Pin_0
  N10: Part1.D6_PWM, S5.Pin_1, S5.Pin_2, R5.Pin_0
  5V: Part1.5V, S1.Pin_3, S1.Pin_4, S2.Pin_3, S2.Pin_4, S3.Pin_3, S3.Pin_4, S4.Pin_3, S4.Pin_4, S5.Pin_3, S5.Pin_4, S6.Pin_3, S6.Pin_4, J1.vcc
  N11: LED1.anode, R8.Pin_0
  N12: LED2.anode, R7.Pin_0

notes:
  1 2 3 4 5 6
